# Fritzing sketch AA-Robot_1 (saved by Fritzing 0.9.3b)

parts:
  Part1 = Arduino Uno (Rev3)  # not connected
  U1 = 2-Channel 5v Relay Shield [package=relay-2ch5v10a]
  M2 = DC Motor
  M1 = DC Motor
  M6 = DC Motor
  U2 = 2-Channel 5v Relay Shield [package=relay-2ch5v10a]
  M7 = DC Motor
  U3 = 2-Channel 5v Relay Shield [package=relay-2ch5v10a]
  VCC1 = Battery

nets:
  N1: U1.K1-In, U3.K1-On
  N2: U1.K1-Off, U1.K2-On, M2.pin_1, M1.pin_1
  N3: U1.K1-On, U1.K2-Off, M2.pin_2, M1.pin_2
  N4: U1.K2-In, U2.K2-In, VCC1.-
  N5: M6.pin_1, U2.K1-On, U2.K2-Off, M7.pin_1
  N6: M6.pin_2, U2.K1-Off, U2.K2-On, M7.pin_2
  N7: U2.K1-In, U3.K2-On
  N8: U3.K1-In, U3.K2-In, VCC1.+

custom parts:
  2-Channel 5v Relay Shield: 2 Channel 5v Relay Shield w. 2x SPD-06VDC-SD-C
